// Digital circuit busdir_inta.dig as structural Verilog
module busdir_inta (
  input  nM1,
  input  nIORQ,
  input  nRD,
  output nINTA,
  output nBUSDIR
);

  or or_1 (nINTA, nM1, nIORQ);
  and and_1 (nBUSDIR, nRD, nINTA);

  // Notes on the sheet:
  //   nM1: default 1
  //   nIORQ: default 1
  //   nRD: default 1
endmodule
