// Digital circuit bdir_bc1.dig as structural Verilog
module bdir_bc1 (
  input  A0,
  input  A1,
  input  nPSG_CS,
  input  CLK,
  output PSG_BC1,
  output PSG_BDIR
);

  wire d_ff_as_1_q, d_ff_as_2_nq, nor_1_out, not_1_out, or_1_out, x;

  or or_1 (or_1_out, x, nPSG_CS);
  nor nor_1 (nor_1_out, nPSG_CS, nPSG_CS);
  not not_1 (not_1_out, CLK);
  nor nor_2 (PSG_BC1, A0, or_1_out);
  nor nor_3 (PSG_BDIR, A1, or_1_out);
  D_FF_AS d_ff_as_1 (.Set(1'b1), .D(nor_1_out), .C(not_1_out), .Clr(nor_1_out), .Q(d_ff_as_1_q));  // open: nQ
  D_FF_AS d_ff_as_2 (.Set(1'b1), .D(d_ff_as_1_q), .C(not_1_out), .Clr(nor_1_out), .nQ(d_ff_as_2_nq));  // open: Q
  nor nor_4 (x, d_ff_as_2_nq, not_1_out);

  // Notes on the sheet:
  //   nPSG_CS: default 1
endmodule
