// Digital circuit bdir_bc1_a2.dig as structural Verilog
module bdir_bc1_a2 (
  input  A2,
  input  PSG_BC1,
  input  PSG_BDIR,
  output PSG1_BC1,
  output PSG1_BDIR,
  output PSG2_BC1,
  output PSG2_BDIR
);

  wire not_1_out;

  not not_1 (not_1_out, A2);
  and and_1 (PSG1_BC1, not_1_out, PSG_BC1);
  and and_2 (PSG1_BDIR, not_1_out, PSG_BDIR);
  and and_3 (PSG2_BC1, A2, PSG_BC1);
  and and_4 (PSG2_BDIR, A2, PSG_BDIR);
endmodule
