// Digital circuit 74155.dig as structural Verilog
module _74155 (
  input  Ea1,
  input  Ea2,
  input  A0,
  input  A1,
  input  Eb1,
  input  Eb2,
  output Q0a,
  output Q1a,
  output Q2a,
  output Q3a,
  output Q0b,
  output Q1b,
  output Q2b,
  output Q3b
);

  wire and_1_out, and_2_out, not_1_out, not_2_out, not_3_out, not_4_out, not_5_out;

  not not_1 (not_1_out, Ea1);
  not not_2 (not_2_out, A1);
  not not_3 (not_3_out, A0);
  and and_1 (and_1_out, ~Ea2, ~not_1_out);  // And
  not not_4 (not_4_out, not_2_out);
  not not_5 (not_5_out, not_3_out);
  and and_2 (and_2_out, ~Eb2, ~Eb1);  // And
  nand nand_1 (Q0a, not_2_out, not_3_out, and_1_out);
  nand nand_2 (Q1a, not_2_out, not_5_out, and_1_out);
  nand nand_3 (Q2a, not_4_out, not_3_out, and_1_out);
  nand nand_4 (Q3a, not_4_out, not_5_out, and_1_out);
  nand nand_5 (Q0b, not_2_out, not_3_out, and_2_out);
  nand nand_6 (Q1b, not_2_out, not_5_out, and_2_out);
  nand nand_7 (Q2b, not_4_out, not_3_out, and_2_out);
  nand nand_8 (Q3b, not_4_out, not_5_out, and_2_out);

  // Notes on the sheet:
  //   Ea1: pin 1
  //   Ea2: pin 2, default 1
  //   A0: pin 13
  //   A1: pin 3
  //   Eb1: pin 14, default 1
  //   Eb2: pin 15
  //   Q0a: pin 7
  //   Q1a: pin 6
  //   Q2a: pin 5
  //   Q3a: pin 4
  //   Q0b: pin 9
  //   Q1b: pin 10
  //   Q2b: pin 11
  //   Q3b: pin 12
endmodule

/* Test case Input 1:
A1 A0 Ea2 Ea1 Q0a Q1a Q2a Q3a
X  X  1   X   1   1   1   1
0  0  0   1   0   1   1   1
0  1  0   1   1   0   1   1
1  0  0   1   1   1   0   1
1  1  0   1   1   1   1   0
X  X  X   0   1   1   1   1



   
*/

/* Test case Input 2:
A1 A0 Eb1 Eb2 Q0b Q1b Q2b Q3b
X  X 1   X   1   1   1   1
0  0 0   0   0   1   1   1
0  1 0   0   1   0   1   1
1  0 0   0   1   1   0   1
1  1 0   0   1   1   1   0
X  X X   1   1   1   1   1
*/

/* Test case Combined Input:
Eb2 Ea1 A1 A0 Ea2 Eb1   Q0b Q1b Q2b Q3b Q0a Q1a Q2a Q3a
X   X   X  X 1   1     1   1   1   1   1   1   1   1
0   0   0  0 0   0     0   1   1   1   1   1   1   1
0   0   0  1 0   0     1   0   1   1   1   1   1   1
0   0   1  0 0   0     1   1   0   1   1   1   1   1
0   0   1  1 0   0     1   1   1   0   1   1   1   1

1   1   0  0 0   0     1   1   1   1   0   1   1   1
1   1   0  1 0   0     1   1   1   1   1   0   1   1
1   1   1  0 0   0     1   1   1   1   1   1   0   1
1   1   1  1 0   0     1   1   1   1   1   1   1   0
*/
