// Digital circuit bus_decode.dig as structural Verilog
module bus_decode (
  input  nIORQ,
  input  nM1,
  input  nRD,
  input  nWR,
  input  nMREQ,
  input  PWR_OK,
  input  nBUSACK,
  input  VCC,
  input  GND,
  input  NC_1,
  input  nRESET0,
  input  NC_11,
  output nINTA,
  output nIOR,
  output nIOW,
  output nMEMR,
  output nMEMW,
  output BUSACK,
  output nDBUS_DIR,
  output nRESET
);

  wire and_1_out, and_2_out, d_ff_as_1_nq, d_ff_as_1_q, or_1_out, or_2_out, or_3_out;

  PowerSupply powersupply_1 (.VDD(VCC), .GND(GND));
  not not_1 (BUSACK, nBUSACK);
  or or_1 (or_1_out, nM1, nIORQ);
  and and_1 (and_1_out, nWR, nRESET);
  D_FF_AS d_ff_as_1 (.Set(~or_1_out), .D(1'b0), .C(1'b0), .Clr(~and_1_out), .Q(d_ff_as_1_q), .nQ(d_ff_as_1_nq));
  and and_2 (and_2_out, ~or_1_out, ~and_1_out);  // And
  or or_2 (or_2_out, d_ff_as_1_nq, and_2_out);
  or or_3 (or_3_out, or_2_out, nRD);
  _74155 _74155_1 (
    .Ea1(or_2_out), .Ea2(nIORQ), .A0(nWR), .A1(nRD), .Eb1(nMREQ), .Eb2(d_ff_as_1_q), .Q1a(nIOR), .Q2a(nIOW),
    .Q1b(nMEMR), .Q2b(nMEMW));  // open: Q0a, Q3a, Q0b, Q3b
  and and_3 (nINTA, or_1_out, or_3_out);
  and and_4 (nRESET, PWR_OK, nRESET0);
  and and_5 (nDBUS_DIR, nMREQ, nINTA);

  // Notes on the sheet:
  //   nIORQ: pin 3, default 1
  //   nM1: pin 4, default 1
  //   nRD: pin 6, default 1
  //   nWR: pin 7, default 1
  //   nMREQ: pin 5, default 1
  //   PWR_OK: pin 8
  //   nINTA: pin 12
  //   nIOR: pin 13
  //   nIOW: pin 14
  //   nMEMR: pin 15
  //   nMEMW: pin 16
  //   nBUSACK: pin 2, default 1
  //   BUSACK: pin 17
  //   nDBUS_DIR: pin 18
  //   VCC: pin 20, default 1
  //   GND: pin 10
  //   NC_1: pin 1
  //   nRESET0: pin 9, default 1
  //   NC_11: pin 11
  //   nRESET: pin 19
endmodule
