// Digital circuit z80_mmu.dig as structural Verilog
module z80_mmu (
  input  [7:0] D_in,
  input  CLK,
  input  nIOWR,
  input  [1:0] R_sel,
  input  nIORD,
  input  A_14,
  input  A_15,
  input  nCS,
  output [7:0] D_out,
  output MA_14,
  output MA_15,
  output MA_16,
  output MA_17,
  output MA_18,
  output MA_19,
  output MA_20,
  output MA_21
);

  wire nclk, or_1_out, or_2_out, rd, wr;
  wire [7:0] registerfile_1_da;

  not not_1 (nclk, CLK);
  or or_1 (or_1_out, nIOWR, nCS);
  or or_2 (or_2_out, nCS, nIORD);
  not not_2 (wr, or_1_out);
  not not_3 (rd, or_2_out);
  RegisterFile #(.Bits(8)) registerfile_1 (
    .Din(D_in), .we(wr), .Rw(R_sel), .C(nclk), .Ra(R_sel), .Rb({A_15, A_14}), .Da(registerfile_1_da),
    .Db({MA_21, MA_20, MA_19, MA_18, MA_17, MA_16, MA_15, MA_14}));
  assign D_out = rd ? registerfile_1_da : 8'bz;  // Driver driver_1

  // Notes on the sheet:
  //   D_out: The data in the specific register.
  //   nIOWR: Write-enable., default 1
  //   R_sel: Register select.
  //   nIORD: Read-enable., default 1
  //   nCS: default 1
endmodule
