// Digital circuit z80_mmu_cs.dig as structural Verilog
module z80_mmu_cs (
  input  A2,
  input  A3,
  input  A4,
  input  A5,
  input  A6,
  input  A7,
  output nMMU_CS
);

  nand nand_1 (nMMU_CS, 1'b1, 1'b1, A2, A3, A4, A5, A6, A7);
endmodule
