// Digital circuit hex_to_7_segment.dig as structural Verilog
module hex_to_7_segment (
  input  [3:0] I,
  input  nBI,
  output SEG_A,
  output SEG_B,
  output SEG_C,
  output SEG_D,
  output SEG_E,
  output SEG_F,
  output SEG_G,
  output DP
);

  ROM #(.AddrBits(5), .Bits(8)) Hex2SevenSegment (
    .A({nBI, I}), .sel(1'b1), .D({DP, SEG_G, SEG_F, SEG_E, SEG_D, SEG_C, SEG_B, SEG_A}));

  // Notes on the sheet:
  //   I: Data input., pin 8,2,3,7
  //   SEG_A: pin 16
  //   SEG_B: pin 15
  //   SEG_C: pin 14
  //   SEG_D: pin 13
  //   SEG_E: pin 12
  //   SEG_F: pin 18
  //   SEG_G: pin 17
  //   DP: pin 19
  //   nBI: pin 5, default 1
  //   contents of Hex2SevenSegment (hex, n*v repeats v):
  //   16*ff,80,f9,a4,b0,99,92,82,f8,80,90,88,83,c6,a1,86,8e
endmodule
