// Digital circuit hex_to_7_segment_top.dig as structural Verilog
module hex_to_7_segment_top (
  input  [3:0] IN,
  input  nBI
);

  wire hex_to_7_segment_1_dp, hex_to_7_segment_1_seg_a, hex_to_7_segment_1_seg_b, hex_to_7_segment_1_seg_c,
       hex_to_7_segment_1_seg_d, hex_to_7_segment_1_seg_e, hex_to_7_segment_1_seg_f, hex_to_7_segment_1_seg_g;

  hex_to_7_segment hex_to_7_segment_1 (
    .I(IN), .nBI(nBI), .SEG_A(hex_to_7_segment_1_seg_a), .SEG_B(hex_to_7_segment_1_seg_b),
    .SEG_C(hex_to_7_segment_1_seg_c), .SEG_D(hex_to_7_segment_1_seg_d), .SEG_E(hex_to_7_segment_1_seg_e),
    .SEG_F(hex_to_7_segment_1_seg_f), .SEG_G(hex_to_7_segment_1_seg_g), .DP(hex_to_7_segment_1_dp));
  Seven_Seg #(.commonConnectionType("anode"), .commonCathode("true")) seven_seg_1 (
    .a(hex_to_7_segment_1_seg_a), .b(hex_to_7_segment_1_seg_b), .c(hex_to_7_segment_1_seg_c),
    .d(hex_to_7_segment_1_seg_d), .e(hex_to_7_segment_1_seg_e), .f(hex_to_7_segment_1_seg_f),
    .g(hex_to_7_segment_1_seg_g), .dp(hex_to_7_segment_1_dp), .common(1'b1));

  // Notes on the sheet:
  //   nBI: default 1
endmodule
