// Digital circuit chiptype_select.dig as structural Verilog
module chiptype_select (
  input  CHIPTYPE_1,
  input  CHIPTYPE_2,
  input  A14,
  input  A15,
  input  nWE,
  output PIN3_CHIP1,
  output PIN3_CHIP2,
  output PIN29_CHIP0,
  output PIN29_CHIP1,
  output PIN31_CHIP0,
  output PIN31_CHIP1
);

  signal_mux CHIPMUX1 (
    .CHIPTYPE(CHIPTYPE_1), .A14(A14), .A15(A15), .nWE(nWE), .PIN3(PIN3_CHIP1), .PIN29(PIN29_CHIP0),
    .PIN31(PIN31_CHIP0));
  signal_mux CHIPMUX2 (
    .CHIPTYPE(CHIPTYPE_2), .A14(A14), .A15(A15), .nWE(nWE), .PIN3(PIN3_CHIP2), .PIN29(PIN29_CHIP1),
    .PIN31(PIN31_CHIP1));

  // Notes on the sheet:
  //   CHIPTYPE_1: pin 5
  //   CHIPTYPE_2: pin 6
  //   A14: pin 2
  //   A15: pin 3
  //   nWE: pin 4, default 1
  //   PIN3_CHIP1: pin 12
  //   PIN3_CHIP2: pin 15
  //   PIN29_CHIP0: pin 13
  //   PIN29_CHIP1: pin 16
  //   PIN31_CHIP0: pin 14
  //   PIN31_CHIP1: pin 17
  //   Chiptype 0: AS6C4008-55PCN (SRAM)
  //   Chiptype 1: SST39SF040 (FLASHROM)
endmodule
