// Digital circuit signal_mux.dig as structural Verilog
module signal_mux (
  input  CHIPTYPE,
  input  A14,
  input  A15,
  input  nWE,
  output PIN3,
  output PIN29,
  output PIN31
);

  Multiplexer multiplexer_1 (.sel(CHIPTYPE), .in_0(A14), .in_1(A15), .out(PIN3));
  Multiplexer multiplexer_2 (.sel(CHIPTYPE), .in_0(nWE), .in_1(A14), .out(PIN29));
  Multiplexer multiplexer_3 (.sel(CHIPTYPE), .in_0(A15), .in_1(1'b1), .out(PIN31));

  // Notes on the sheet:
  //   CHIPTYPE: Chiptype 0: AS6C4008-55PCN (SRAM)
  //   Chiptype 1: SST39SF040 (FLASHROM)
  //   nWE: default 1
  //   Chiptype 0: AS6C4008-55PCN (SRAM)
  //   Chiptype 1: SST39SF040 (FLASHROM)
endmodule
