// Digital circuit flash_rom_a16_a17.dig as structural Verilog
module flash_rom_a16_a17 (
  input  nSUBSLTSL33,
  input  nSUBSLTSL31,
  input  nSUBSLTSL30,
  output A17,
  output A16
);

  wire and_1_out, not_1_out, not_2_out, not_3_out;

  not not_1 (not_1_out, nSUBSLTSL33);
  not not_2 (not_2_out, nSUBSLTSL31);
  not not_3 (not_3_out, nSUBSLTSL30);
  or or_1 (A17, not_2_out, not_1_out);
  and and_1 (and_1_out, not_3_out, nSUBSLTSL31);
  or or_2 (A16, and_1_out, not_1_out);
endmodule
