// Digital circuit flash_rom_selects.dig as structural Verilog
module flash_rom_selects (
  input  nSLTSL0,
  input  nSBSLTSL30,
  input  nSBSLTSL31,
  input  nSBSLTSL33,
  output nROM_CS,
  output ROM_A16,
  output ROM_A17
);

  and and_1 (nROM_CS, nSLTSL0, nSBSLTSL30, nSBSLTSL31, nSBSLTSL33);
  flash_rom_a16_a17 flash_rom_a16_a17_1 (
    .nSUBSLTSL33(nSBSLTSL33), .nSUBSLTSL31(nSBSLTSL31), .nSUBSLTSL30(nSBSLTSL30), .A17(ROM_A17), .A16(ROM_A16));

  // Notes on the sheet:
  //   nSLTSL0: default 1
  //   nSBSLTSL30: default 1
  //   nSBSLTSL31: default 1
  //   nSBSLTSL33: default 1
endmodule
