// Digital circuit mem_req.dig as structural Verilog
module mem_req (
  input  nB_RFSH,
  input  nB_MREQ,
  output nMEM_REQ
);

  wire not_1_out;

  not not_1 (not_1_out, nB_RFSH);
  or or_1 (nMEM_REQ, nB_MREQ, not_1_out);

  // Notes on the sheet:
  //   nB_RFSH: default 1
  //   nB_MREQ: default 1
endmodule
