// Digital circuit ppi_slot_select.dig as structural Verilog
module ppi_slot_select (
  input  [7:0] nCSLH,
  input  nSLTSL_CS,
  input  A14,
  input  A15,
  input  nMEM_REQ,
  output nSLTSL_0,
  output nSLTSL_1,
  output nSLTSL_2,
  output nSLTSL_3
);

  wire _74153_1_pin7, _74153_1_pin9, notconnected_1_out, notconnected_2_out, notconnected_3_out;

  _74153 _74153_1 (
    .pin1(nSLTSL_CS), .pin2(A15), .pin3(nCSLH[6]), .pin4(nCSLH[4]), .pin5(nCSLH[2]), .pin6(nCSLH[0]),
    .pin7(_74153_1_pin7), .pin8(1'b0), .pin9(_74153_1_pin9), .pin10(nCSLH[1]), .pin11(nCSLH[3]),
    .pin12(nCSLH[5]), .pin13(nCSLH[7]), .pin14(A14), .pin15(nSLTSL_CS), .pin16(1'b1));
  // NotConnected on notconnected_1_out
  // NotConnected on notconnected_2_out
  // NotConnected on notconnected_3_out
  _74139 _74139_1 (
    .pin1(notconnected_1_out), .pin2(notconnected_2_out), .pin3(notconnected_3_out), .pin8(1'b0),
    .pin9(nSLTSL_3), .pin10(nSLTSL_2), .pin11(nSLTSL_1), .pin12(nSLTSL_0), .pin13(_74153_1_pin9),
    .pin14(_74153_1_pin7), .pin15(nMEM_REQ), .pin16(1'b1));  // open: pin4, pin5, pin6, pin7

  // Notes on the sheet:
  //   nCSLH: default 228
  //   nSLTSL_CS: default 1
  //   nMEM_REQ: default 1
endmodule
