// Digital circuit ppi_slot_select_address_decoding_analyzed.dig as structural Verilog
module ppi_slot_select_address_decoding_analyzed (
  input  A_7,
  input  A_6,
  input  A_5,
  input  A_4,
  input  A_3,
  input  nB_IORQ,
  input  nB_M1,
  output nPPI_CS
);

  wire not_1_out, not_2_out, not_3_out, not_4_out;

  not not_1 (not_1_out, A_7);
  not not_2 (not_2_out, A_5);
  not not_3 (not_3_out, A_3);
  not not_4 (not_4_out, nB_M1);
  or or_1 (nPPI_CS, not_3_out, A_4, not_2_out, A_6, not_1_out, nB_IORQ, not_4_out);
endmodule
