// Digital circuit ppi_slot_select_analyzed.dig as structural Verilog
module ppi_slot_select_analyzed (
  input  A_7,
  input  A_6,
  input  A_5,
  input  A_4,
  input  A_3,
  input  nB_IORQ,
  input  nB_M1,
  output Y_0,
  output Y_1,
  output Y_2,
  output Y_3,
  output Y_4,
  output Y_5,
  output Y_6,
  output Y_7
);

  wire not_1_out, not_2_out, not_3_out, not_4_out, not_5_out;

  not not_1 (not_1_out, A_7);
  not not_2 (not_2_out, A_5);
  not not_3 (not_3_out, A_4);
  not not_4 (not_4_out, A_3);
  not not_5 (not_5_out, nB_M1);
  or or_1 (Y_0, A_3, A_4, A_5, A_6, not_1_out, nB_IORQ, not_5_out);
  or or_2 (Y_1, not_4_out, A_4, A_5, A_6, not_1_out, nB_IORQ, not_5_out);
  or or_3 (Y_2, A_3, not_3_out, A_5, A_6, not_1_out, nB_IORQ, not_5_out);
  or or_4 (Y_3, not_4_out, not_3_out, A_5, A_6, not_1_out, nB_IORQ, not_5_out);
  or or_5 (Y_4, A_3, A_4, not_2_out, A_6, not_1_out, nB_IORQ, not_5_out);
  or or_6 (Y_5, not_4_out, A_4, not_2_out, A_6, not_1_out, nB_IORQ, not_5_out);
  or or_7 (Y_6, A_3, not_3_out, not_2_out, A_6, not_1_out, nB_IORQ, not_5_out);
  or or_8 (Y_7, not_4_out, not_3_out, not_2_out, A_6, not_1_out, nB_IORQ, not_5_out);
endmodule
