// Digital circuit sltsl_cs.dig as structural Verilog
module sltsl_cs (
  input  nRESET,
  input  nPPI_CS,
  output nSLTSL_CS
);

  RS_FF_AS rs_ff_as_1 (.S(~nRESET), .R(~nPPI_CS), .Q(nSLTSL_CS));  // open: nQ

  // Notes on the sheet:
  //   nRESET: default 1
  //   nPPI_CS: default 1
endmodule
