// Digital circuit ppi_slot_select.dig as structural Verilog
module ppi_slot_select (
  input  [7:0] nCSLH,
  input  nSLTSL_CS,
  input  A14,
  input  A15,
  input  nMEM_REQ,
  output nSLTSL_0,
  output nSLTSL_1,
  output nSLTSL_2,
  output nSLTSL_3
);

  wire and_1_out, and_2_out, and_3_out, and_4_out, and_5_out, and_6_out, and_7_out, and_8_out, and_9_out,
       and_10_out, and_11_out, and_12_out, and_13_out, and_14_out, and_15_out, and_16_out, and_17_out,
       and_18_out, and_19_out, and_20_out, and_21_out, and_22_out, and_23_out, and_24_out, and_25_out,
       and_26_out, and_27_out, and_28_out, and_29_out, and_30_out, and_31_out, and_32_out, not_1_out,
       not_2_out, not_3_out, not_4_out, not_5_out, not_6_out, not_7_out, not_8_out, not_9_out, not_10_out,
       not_11_out;

  not not_1 (not_1_out, nCSLH[7]);
  not not_2 (not_2_out, nCSLH[6]);
  not not_3 (not_3_out, nCSLH[5]);
  not not_4 (not_4_out, nCSLH[4]);
  not not_5 (not_5_out, nCSLH[3]);
  not not_6 (not_6_out, nCSLH[2]);
  not not_7 (not_7_out, nCSLH[1]);
  not not_8 (not_8_out, nCSLH[0]);
  not not_9 (not_9_out, nSLTSL_CS);
  not not_10 (not_10_out, A14);
  not not_11 (not_11_out, A15);
  and and_1 (and_1_out, not_10_out, not_11_out, nCSLH[0], not_9_out);
  and and_2 (and_2_out, not_10_out, not_11_out, nCSLH[1], not_9_out);
  and and_3 (and_3_out, A14, not_11_out, nCSLH[2], not_9_out);
  and and_4 (and_4_out, A14, not_11_out, nCSLH[3], not_9_out);
  and and_5 (and_5_out, not_10_out, A15, nCSLH[4], not_9_out);
  and and_6 (and_6_out, not_10_out, A15, nCSLH[5], not_9_out);
  and and_7 (and_7_out, A14, A15, nCSLH[6], not_9_out);
  and and_8 (and_8_out, A14, A15, nCSLH[7], not_9_out);
  and and_9 (and_9_out, not_10_out, not_11_out, not_8_out);
  and and_10 (and_10_out, not_10_out, not_11_out, nCSLH[1]);
  and and_11 (and_11_out, A14, not_11_out, not_6_out);
  and and_12 (and_12_out, A14, not_11_out, nCSLH[3]);
  and and_13 (and_13_out, not_10_out, A15, not_4_out);
  and and_14 (and_14_out, not_10_out, A15, nCSLH[5]);
  and and_15 (and_15_out, A14, A15, not_2_out);
  and and_16 (and_16_out, A14, A15, nCSLH[7]);
  and and_17 (and_17_out, not_10_out, not_11_out, nCSLH[0]);
  and and_18 (and_18_out, not_10_out, not_11_out, not_7_out);
  and and_19 (and_19_out, A14, not_11_out, nCSLH[2]);
  and and_20 (and_20_out, A14, not_11_out, not_5_out);
  and and_21 (and_21_out, not_10_out, A15, nCSLH[4]);
  and and_22 (and_22_out, not_10_out, A15, not_3_out);
  and and_23 (and_23_out, A14, A15, nCSLH[6]);
  and and_24 (and_24_out, A14, A15, not_1_out);
  and and_25 (and_25_out, not_10_out, not_11_out, not_8_out);
  and and_26 (and_26_out, not_10_out, not_11_out, not_7_out);
  and and_27 (and_27_out, A14, not_11_out, not_6_out);
  and and_28 (and_28_out, A14, not_11_out, not_5_out);
  and and_29 (and_29_out, not_10_out, A15, not_4_out);
  and and_30 (and_30_out, not_10_out, A15, not_3_out);
  and and_31 (and_31_out, A14, A15, not_2_out);
  and and_32 (and_32_out, A14, A15, not_1_out);
  or or_1 (nSLTSL_0, and_1_out, and_2_out, and_3_out, and_4_out, and_5_out, and_6_out, and_7_out, and_8_out, nMEM_REQ);
  or or_2 (nSLTSL_1, and_9_out, and_10_out, and_11_out, and_12_out, and_13_out, and_14_out, and_15_out, and_16_out, nMEM_REQ, nSLTSL_CS);
  or or_3 (nSLTSL_2, and_17_out, and_18_out, and_19_out, and_20_out, and_21_out, and_22_out, and_23_out, and_24_out, nMEM_REQ, nSLTSL_CS);
  or or_4 (nSLTSL_3, and_25_out, and_26_out, and_27_out, and_28_out, and_29_out, and_30_out, and_31_out, and_32_out, nMEM_REQ, nSLTSL_CS);

  // Other names for the same wires on the sheet: nCSLH_0 = nCSLH[0]; nCSLH_1 = nCSLH[1]; nCSLH_2 = nCSLH[2];
  //   nCSLH_3 = nCSLH[3]; nCSLH_4 = nCSLH[4]; nCSLH_5 = nCSLH[5]; nCSLH_6 = nCSLH[6]; nCSLH_7 = nCSLH[7]
endmodule
