// Digital circuit chip_selects.dig as structural Verilog
module chip_selects (
  input  nM1,
  input  nMREQ,
  input  nIORQ,
  input  nRESET,
  input  [5:0] A,
  input  nCS,
  output RESET,
  output nPPI_CS,
  output nUART_CS,
  output nIO_OP,
  output nMEM_OP
);

  wire cs, iorq, m1, mreq, na_2, na_3, na_4, na_5, na_6, na_7;

  not not_1 (RESET, nRESET);
  not not_2 (m1, nM1);
  not not_3 (mreq, nMREQ);
  not not_4 (iorq, nIORQ);
  not not_5 (cs, nCS);
  not not_6 (na_2, A[0]);
  not not_7 (na_3, A[1]);
  not not_8 (na_4, A[2]);
  not not_9 (na_5, A[3]);
  not not_10 (na_6, A[4]);
  not not_11 (na_7, A[5]);
  or or_1 (nIO_OP, nIORQ, m1, mreq);
  or or_2 (nMEM_OP, iorq, nMREQ);
  or or_3 (nPPI_CS, A[0], na_3, A[2], na_5, A[4], na_7, cs, nIO_OP);
  or or_4 (nUART_CS, A[1], A[2], A[3], A[4], na_7, cs, nIO_OP);

  // Other names for the same wires on the sheet: a_2 = A[0]; a_3 = A[1]; a_4 = A[2]; a_5 = A[3]; a_6 = A[4];
  //   a_7 = A[5]

  // Notes on the sheet:
  //   nM1: pin 3, default 1
  //   nMREQ: pin 4, default 1
  //   nIORQ: pin 5, default 1
  //   nRESET: pin 2, default 1
  //   A: Address bus., pin 7,8,9,10,11,13
  //   RESET: pin 23
  //   nPPI_CS: pin 22
  //   nUART_CS: pin 21
  //   nCS: Chip select signal., pin 6
  //   nIO_OP: pin 20
  //   nMEM_OP: pin 19
endmodule
