// Digital circuit hi_addr.dig as structural Verilog
module hi_addr (
  input  A_8,
  input  A_9,
  input  A_10,
  input  A_11,
  input  A_12,
  input  A_13,
  input  A_14,
  input  A_15,
  output nHI_ADDR,
  output FFxx
);

  nor nor_1 (nHI_ADDR, A_8, A_9, A_10, A_11, A_12, A_13, A_14, A_15);
  nand nand_1 (FFxx, A_15, A_14, A_13, A_12, A_11, A_10, A_9, A_8);

  // Notes on the sheet:
  //   A_8: pin 2
  //   A_9: pin 3
  //   A_10: pin 4
  //   A_11: pin 5
  //   A_12: pin 6
  //   A_13: pin 7
  //   A_14: pin 8
  //   A_15: pin 9
  //   nHI_ADDR: pin 23
  //   FFxx: pin 22
endmodule
