// Digital circuit 8259_cs.dig as structural Verilog
module _8259_cs (
  input  nIOW,
  input  nIOR,
  input  [7:0] A,
  output nCS
);

  wire not_1_out, not_2_out, not_3_out, not_4_out, not_5_out, or_1_out;

  not not_1 (not_1_out, nIOW);
  not not_2 (not_2_out, nIOR);
  or or_1 (or_1_out, not_1_out, not_2_out);
  nand nand_1 (nCS, or_1_out, not_3_out, not_4_out, not_5_out, A[4], A[5], A[6], A[7]);
  not not_3 (not_3_out, A[1]);
  not not_4 (not_4_out, A[2]);
  not not_5 (not_5_out, A[3]);

  // Notes on the sheet:
  //   nIOW: default 1
  //   nIOR: default 1
endmodule
