// Digital circuit im2_int_cntrlr.dig as structural Verilog
module im2_int_cntrlr (
  input  nINT_0,
  input  nINT_1,
  input  nINT_2,
  input  nINT_3,
  input  nINT_4,
  input  nINT_5,
  input  nINT_6,
  input  nINT_7,
  input  nM1,
  input  nIORQ,
  output D_0,
  output D_1,
  output D_2,
  output D_3,
  output D_4,
  output D_5,
  output D_6,
  output D_7,
  output nINTA,
  output nCPU_INT
);

  wire not_1_out, not_2_out, not_3_out, ns0, ns1, ns2, or_2_out;

  _74148 _74148_1 (
    .pin1(nINT_4), .pin2(nINT_5), .pin3(nINT_6), .pin4(nINT_7), .pin5(1'b0), .pin6(ns2), .pin7(ns1),
    .pin8(1'b0), .pin9(ns0), .pin10(nINT_0), .pin11(nINT_1), .pin12(nINT_2), .pin13(nINT_3),
    .pin14(nCPU_INT), .pin16(1'b1));  // open: pin15
  or or_1 (nINTA, nM1, nIORQ);
  or or_2 (or_2_out, nINTA, nCPU_INT);
  not not_1 (not_1_out, ns0);
  not not_2 (not_2_out, ns1);
  not not_3 (not_3_out, ns2);
  _74573 _74573_1 (
    .pin1(or_2_out), .pin2(1'b0), .pin3(not_1_out), .pin4(not_2_out), .pin5(not_3_out), .pin6(1'b0),
    .pin7(1'b0), .pin8(1'b0), .pin9(1'b0), .pin10(1'b0), .pin11(nM1), .pin12(D_7), .pin13(D_6), .pin14(D_5),
    .pin15(D_4), .pin16(D_3), .pin17(D_2), .pin18(D_1), .pin19(D_0), .pin20(1'b1));

  // Other names for the same wires on the sheet: nim2_int = nCPU_INT; nint0 = nINT_0; nint1 = nINT_1; nint2 = nINT_2;
  //   nint3 = nINT_3; nint4 = nINT_4; nint5 = nINT_5; nint6 = nINT_6; nint7 = nINT_7

  // Notes on the sheet:
  //   nINT_0: default 1
  //   nINT_1: default 1
  //   nINT_2: default 1
  //   nINT_3: default 1
  //   nINT_4: default 1
  //   nINT_5: default 1
  //   nINT_6: default 1
  //   nINT_7: default 1
  //   nM1: default 1
  //   nIORQ: default 1
endmodule
