// Digital circuit im2_int_cntrlr_test.dig as structural Verilog
module im2_int_cntrlr_test (
  input  clk
);

  wire _4_out, _5_out, _6_out, _7_out, DOWN_out, im2_int_cntrlr_1_ncpu_int, im2_int_cntrlr_1_ninta, LEFT_out,
       m1_iorq_gen_1_niorq, m1_iorq_gen_1_nm1, not_1_out, not_2_out, RIGHT_out, UP_out;
  wire [3:0] im2_int_cntrlr_1_d_0, INTNO_2_q;

  Button #(.activeLow("true")) UP (.out(UP_out));
  Button #(.activeLow("true")) DOWN (.out(DOWN_out));
  Button #(.activeLow("true")) LEFT (.out(LEFT_out));
  Button #(.activeLow("true")) RIGHT (.out(RIGHT_out));
  Button #(.activeLow("true")) _4 (.out(_4_out));
  Button #(.activeLow("true")) _5 (.out(_5_out));
  Button #(.activeLow("true")) _6 (.out(_6_out));
  Button #(.activeLow("true")) _7 (.out(_7_out));
  m1_iorq_gen m1_iorq_gen_1 (
    .CLK(clk), .nINT(im2_int_cntrlr_1_ncpu_int), .nIORQ(m1_iorq_gen_1_niorq), .nM1(m1_iorq_gen_1_nm1));
  // Probe ~{M1} on m1_iorq_gen_1_nm1
  im2_int_cntrlr im2_int_cntrlr_1 (
    .nINT_0(UP_out), .nINT_1(DOWN_out), .nINT_2(LEFT_out), .nINT_3(RIGHT_out), .nINT_4(_4_out),
    .nINT_5(_5_out), .nINT_6(_6_out), .nINT_7(_7_out), .nM1(m1_iorq_gen_1_niorq), .nIORQ(m1_iorq_gen_1_nm1),
    .D_0(im2_int_cntrlr_1_d_0[0]), .D_1(im2_int_cntrlr_1_d_0[1]), .D_2(im2_int_cntrlr_1_d_0[2]),
    .D_3(im2_int_cntrlr_1_d_0[3]), .nINTA(im2_int_cntrlr_1_ninta), .nCPU_INT(im2_int_cntrlr_1_ncpu_int));  // open: D_4, D_5, D_6, D_7
  // Probe intno on im2_int_cntrlr_1_d_0
  Register #(.Bits(4)) INTNO_2 (.D(im2_int_cntrlr_1_d_0), .C(im2_int_cntrlr_1_ninta), .en(1'b1), .Q(INTNO_2_q));
  not not_1 (not_1_out, im2_int_cntrlr_1_ninta);
  not not_2 (not_2_out, im2_int_cntrlr_1_ncpu_int);
  Seven_Seg_Hex seven_seg_hex_1 (.d(INTNO_2_q), .dp(1'b0));
  LED nINTA (.in(not_1_out));
  LED nCPU_INT (.in(not_2_out));
endmodule
