// Digital circuit m1_iorq_gen.dig as structural Verilog
module m1_iorq_gen (
  input  CLK,
  input  nINT,
  output nIORQ,
  output nM1
);

  wire cntclr, niffout, niffset;
  wire [2:0] cmpval, T_out;

  Counter #(.Bits(3)) T (.en(1'b1), .C(CLK), .clr(cntclr), .out(T_out));  // open: ovf
  RS_FF IFF (.S(~niffset), .C(CLK), .R(cntclr), .nQ(niffout));  // open: Q
  Multiplexer #(.Bits(3)) multiplexer_1 (.sel(niffout), .in_0(3'b101), .in_1(3'b011), .out(cmpval));
  Comparator #(.Bits(3)) comparator_1 (.a(T_out), .b(cmpval), .eq(cntclr));  // open: gt, lt
  Multiplexer #(.Selector_Bits(3)) multiplexer_2 (
    .sel(T_out), .in_0(1'b1), .in_1(1'b1), .in_2(niffout), .in_3(niffout), .in_4(1'b1), .in_5(1'b1),
    .in_6(1'b1), .in_7(1'b1), .out(nIORQ));
  Multiplexer #(.Selector_Bits(3)) multiplexer_3 (
    .sel(T_out), .in_0(1'b0), .in_1(1'b0), .in_2(niffout), .in_3(niffout), .in_4(1'b1), .in_5(1'b1),
    .in_6(1'b1), .in_7(1'b1), .out(nM1));
  Multiplexer #(.Selector_Bits(3)) multiplexer_4 (
    .sel(T_out), .in_0(1'b1), .in_1(1'b1), .in_2(1'b1), .in_3(nINT), .in_4(nINT), .in_5(nINT), .in_6(nINT),
    .in_7(nINT), .out(niffset));

  // Notes on the sheet:
  //   nINT: default 1
endmodule
