// Digital circuit intctrl.dig as structural Verilog
module intctrl (
  input  nM1,
  input  nIORQ,
  input  nINT_0,
  input  nINT_1,
  input  nINT_2,
  input  nINT_3,
  input  nINT_4,
  input  nINT_5,
  input  nINT_6,
  input  nINT_7,
  output nINT,
  output [7:0] Q
);

  wire _74148_1_pin6, _74148_1_pin7, _74148_1_pin9, _74148_1_pin14, ninta, nintack;

  _74148 _74148_1 (
    .pin1(nINT_4), .pin2(nINT_5), .pin3(nINT_6), .pin4(nINT_7), .pin5(1'b0), .pin6(_74148_1_pin6),
    .pin7(_74148_1_pin7), .pin8(1'b0), .pin9(_74148_1_pin9), .pin10(nINT_0), .pin11(nINT_1), .pin12(nINT_2),
    .pin13(nINT_3), .pin14(_74148_1_pin14), .pin16(1'b1));  // open: pin15
  or or_1 (ninta, nM1, nIORQ);
  _74573 _74573_1 (
    .pin1(nintack), .pin2(1'b0), .pin3(_74148_1_pin9), .pin4(_74148_1_pin7), .pin5(_74148_1_pin6),
    .pin6(1'b0), .pin7(1'b0), .pin8(1'b0), .pin9(1'b0), .pin10(1'b0), .pin11(nM1), .pin12(Q[7]),
    .pin13(Q[6]), .pin14(Q[5]), .pin15(Q[4]), .pin16(Q[3]), .pin17(Q[2]), .pin18(Q[1]), .pin19(Q[0]),
    .pin20(1'b1));
  or or_2 (nintack, ninta, _74148_1_pin14);
  assign nINT = 1'b1 ? _74148_1_pin14 : 1'bz;  // Driver driver_1

  // Notes on the sheet:
  //   Q: Data output.
  //   nM1: default 1
  //   nIORQ: default 1
  //   nINT_0: default 1
  //   nINT_1: default 1
  //   nINT_2: default 1
  //   nINT_3: default 1
  //   nINT_4: default 1
  //   nINT_5: default 1
  //   nINT_6: default 1
  //   nINT_7: default 1
endmodule
