// Digital circuit ls139_as_an_inverter.dig as structural Verilog
module ls139_as_an_inverter (
  input  nRESET,
  output RESET
);

  wire _74139_1_pin13, _74139_1_pin14, _74139_1_pin15;

  _74139 _74139_1 (
    .pin1(1'b0), .pin2(nRESET), .pin3(1'b1), .pin7(RESET), .pin8(1'b0), .pin13(_74139_1_pin13),
    .pin14(_74139_1_pin14), .pin15(_74139_1_pin15), .pin16(1'b1));  // open: pin4, pin5, pin6, pin9, pin10, pin11, pin12
  // NotConnected on _74139_1_pin15
  // NotConnected on _74139_1_pin14
  // NotConnected on _74139_1_pin13

  // Notes on the sheet:
  //   nRESET: default 1
endmodule
