// Digital circuit reset_clk.dig as structural Verilog
module reset_clk (
  input  nRESET_SW,
  input  PRW_OK,
  output nRESET
);

  and and_1 (nRESET, nRESET_SW, PRW_OK);

  // Notes on the sheet:
  //   nRESET_SW: default 1
endmodule
