// Digital circuit slt_sel.dig as structural Verilog
module slt_sel (
  input  PA_0,
  input  PA_1,
  input  PA_2,
  input  PA_3,
  input  PA_4,
  input  PA_5,
  input  PA_6,
  input  PA_7,
  input  nCS,
  input  [15:0] A,
  output SLOT_A,
  output SLOT_B
);

  _74153 _74153_1 (
    .pin1(nCS), .pin2(A[15]), .pin3(PA_6), .pin4(PA_4), .pin5(PA_2), .pin6(PA_0), .pin7(SLOT_A), .pin8(1'b0),
    .pin9(SLOT_B), .pin10(PA_1), .pin11(PA_3), .pin12(PA_5), .pin13(PA_7), .pin14(A[14]), .pin15(nCS),
    .pin16(1'b1));

  // Notes on the sheet:
  //   nCS: default 1
endmodule
